# Fritzing sketch proj-temp-DS18B20 (saved by Fritzing 0.9.5d)

parts:
  M1 = DOIT Esp32 DevKit v1 (30 pins long, 11 pins width) [part_number=ESP32S-PIN30]
  A1 = BBAA100043
  GSM_SIM_GPSR_SMS_SIM900_SIM1 = SIM800L [package=THT]
  DS1 = DS18B20 1-Wire Temperature Sensor Probe
  A2 = MH-FMD buzzer
  M2 = MT3608 Module
  C1 = Electrolytic Capacitor [capacitance=1000µF package="300 mil [THT, electrolytic]"]
  C3 = Electrolytic Capacitor [capacitance=1000μF package="1010 [SMD, electrolytic]"]

nets:
  GND: M1.GND, A1.pin4, DS1.GND, A2.Pin_3, M2.pin1, C3.-
  N1: M1.D4, DS1.DQ
  N2: M1.D32, GSM_SIM_GPSR_SMS_SIM900_SIM1.SIM_TXD
  N3: M1.D33, GSM_SIM_GPSR_SMS_SIM900_SIM1.SIM_RXD
  N4: M1.D25, A1.pin1
  N5: M1.D26, A1.pin2
  N6: M1.D27, A1.pin3
  N7: M1.D13, A2.Pin_2
  VIN: M1.VIN, DS1.VDD, A2.Pin_1, M2.pin2, C3.+
  N8: GSM_SIM_GPSR_SMS_SIM900_SIM1.5V, M2.pin3, C1.+
  N9: GSM_SIM_GPSR_SMS_SIM900_SIM1.GND, M2.pin4, C1.-

notes:
  DS18B20
  Temperature Sensor Probe
  ESP32
  Microcontroller
  SIM800L EVB
  GSM Module with
  1000uF capacitor
  4.4v-out Boost Converter Module with
  470uF capacitor
  RGY LED Module
  Buzzer Module

custom parts:
  DOIT Esp32 DevKit v1 (30 pins long, 11 pins width): The DOIT Esp32 DevKit v1 is one of the development board created by DOIT to evaluate the ESP-WROOM-32 module. It is based on the ESP32 microcontroller that boasts Wifi, Bluetooth, Ethernet and Low Power support all in a single chip. (vanepp) made breadboard work, adjusted pin numbering and labels and reduced size of schematic and cleaned up pcb. This chip is 30pins long (2 x15) and 11 pins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
  BBAA100043: BBAA100043 traffic light module.
  MH-FMD buzzer: MH-FMD buzzer.
  MT3608 Module: MT3608 Boost Converter Module Links: Aerosemi MT3608 2A Step Up Converter datasheet
